# Fritzing sketch diagram (saved by Fritzing 0.9.9b)
breadboards: 2

parts:
  Part1 = Arduino Uno (Rev3) - ICSP
  LED1 = LED - 5mm [color="Red (633nm)" current=0.030 package="5 mm [THT]"]
  R1 = Resistor [tolerance=±5% resistance=220 package="2512 [SMD]"]
  LED2 = LED - 5mm [color="Green (555nm)" current=0.030 package="5 mm [THT]"]
  R2 = Resistor [tolerance=±5% resistance=220 package="2512 [SMD]"]
  R3 = PHOTOCELL [package=photocell]
  R4 = Resistor [tolerance=±5% resistance=10k package="2512 [SMD]"]
  S2 = Pushbutton [package="[THT]"]
  S1 = Pushbutton [package="[THT]"]

nets:
  N1: Part1.A0, R3.P$1, R4.Pin_1
  N2: Part1.A2, LED2.cathode, R2.Pin_1
  N3: Part1.A3, LED1.cathode, R1.Pin_1
  N4: Part1.ICSP_MISO, Part1.D12/MISO, S1.Pin_1, S1.Pin_2
  N5: Part1.ICSP_MOSI, Part1.D11_PWM/MOSI, S2.Pin_1, S2.Pin_2
  N6: Part1.GND, R1.Pin_0, R2.Pin_0, R4.Pin_0, S2.Pin_3, S2.Pin_4, S1.Pin_3, S1.Pin_4
  N7: Part1.D9_PWM, LED1.anode
  N8: Part1.D10_PWM/SS, LED2.anode
  N9: Part1.5V, R3.P$2
